# Fritzing sketch debtron_circuitry (saved by Fritzing 0.9.2b)
stripboards: 1
perfboards: 1

parts:
  Part1 = Arduino Uno (Rev3)
  R4 = Rotary Potentiometer (Small) [maximum_resistance=1kΩ package=THT]
  R3 = Rotary Potentiometer (Small) [maximum_resistance=1kΩ package=THT]
  R2 = Rotary Potentiometer (Small) [maximum_resistance=1kΩ package=THT]
  R1 = Rotary Potentiometer (Small) [maximum_resistance=1kΩ package=THT]
  R0 = Rotary Potentiometer (Small) [maximum_resistance=1kΩ package=THT]
  R5 = Rotary Potentiometer (Small) [maximum_resistance=1kΩ package=THT]
  VIDEO = Resistor [tolerance=±5% resistance=220 package=THT]
  SYNC = Resistor [tolerance=±2% resistance=1k package=THT]
  J1 = Piezo Speaker

nets:
  N1: Part1.A0, R0.wiper
  N2: Part1.A1, R1.wiper
  N3: Part1.A2, R2.wiper
  N4: Part1.A3, R3.wiper
  N5: Part1.A4/SDA, R4.wiper
  N6: Part1.A5/SCL, R5.wiper
  N7: Part1.D9_PWM, SYNC.Pin_0
  N8: Part1.D10_PWM/SS, J1.pin2
  N9: Part1.GND, R4.leg2, R3.leg2, R2.leg2, R1.leg2, R0.leg2, R5.leg2, J1.pin1
  N10: Part1.D7, VIDEO.Pin_0
  N11: Part1.5V, R4.leg1, R3.leg1, R2.leg1, R1.leg1, R0.leg1, R5.leg1
  N12: VIDEO.Pin_1, SYNC.Pin_1

notes:
  RCA shield (outer)
  RCA signal (inner)
